# Fritzing sketch brb4bbb (saved by Fritzing 0.9.4)
breadboards: 1

parts:
  Arduino_Micro = Arduino Micro (Rev3)
  R1 = Resistor [tolerance=±5% resistance=220 package=THT]
  S1 = Pushbutton [package="[THT]"]
  LED1 = LED - 5mm [color="Red (633nm)" package="5 mm [THT]"]

nets:
  N1: Arduino_Micro.GND, S1.Pin_3, S1.Pin_4, LED1.cathode
  N2: Arduino_Micro.D2/SDA, R1.Pin_0
  N3: Arduino_Micro.D3/SCL, S1.Pin_1, S1.Pin_2
  N4: R1.Pin_1, LED1.anode
